# Fritzing sketch esquema_led_rgb_potenciometro (saved by Fritzing 0.9.3b)
breadboards: 1

parts:
  Componente1 = Arduino Uno (Rev3)
  R1 = Rotary Potentiometer (Small) [maximum_resistance=100kΩ package=THT]
  R2 = Rotary Potentiometer (Small) [maximum_resistance=100kΩ package=THT]
  R3 = Rotary Potentiometer (Small) [maximum_resistance=100kΩ package=THT]
  R4 = Resistor [tolerance=±5% resistance=330k package=THT]
  R5 = Resistor [tolerance=±5% resistance=330k package=THT]
  R6 = Resistor [tolerance=±5% resistance=330k package=THT]
  R7 = Resistor [tolerance=±5% resistance=330k package=THT]
  R8 = Resistor [tolerance=±5% resistance=330k package=THT]
  R9 = Resistor [tolerance=±5% resistance=330k package=THT]
  LED1 = RGB LED (com. cathode, rgb) [package="5 mm [THT]"]  # not connected

nets:
  N1: Componente1.A0, R1.wiper
  N2: Componente1.A1, R2.wiper
  N3: Componente1.A2, R3.wiper
  N4: Componente1.GND, R1.leg2, R2.leg2, R3.leg2
  N5: Componente1.D3_PWM, R7.Pin_1
  N6: Componente1.D5_PWM, R9.Pin_1
  N7: Componente1.D6_PWM, R8.Pin_1
  N8: Componente1.5V, R4.Pin_1, R5.Pin_1, R6.Pin_1
  N9: R1.leg1, R4.Pin_0
  N10: R2.leg1, R5.Pin_0
  N11: R3.leg1, R6.Pin_0

notes:
  Pode ligar mais um LED RGB, só colocar no mesmo espaço de maneira vertical
  Verifique os pinos do LED e a correspondência com as cores
