# Fritzing sketch esquema_led_simples_python (saved by Fritzing 0.9.3b)
breadboards: 1

parts:
  Componente1 = Arduino Uno (Rev3)
  LED1 = LED - 5mm [color="Red (633nm)" package="5 mm [THT]"]
  LED2 = LED - 5mm [color="Yellow (595nm)" package="5 mm [THT]"]
  LED3 = LED - 5mm [color="Green (555nm)" package="5 mm [THT]"]

nets:
  N1: Componente1.D10_PWM/SS, LED1.anode
  N2: Componente1.D11_PWM/MOSI, LED3.anode
  N3: Componente1.D12/MISO, LED2.anode
  N4: Componente1.GND, LED1.cathode, LED2.cathode, LED3.cathode

notes:
  Atenção: No Arduino IDE é preciso carregar o firmware do firmata.
