# Fritzing sketch esquema_pontuacao (saved by Fritzing 0.9.3b)
breadboards: 1

parts:
  Componente1 = Arduino Uno (Rev3)
  LED1 = LED - 5mm [color="Red (633nm)" package="5 mm [THT]"]
  LED2 = LED - 5mm [color="Red (633nm)" package="5 mm [THT]"]
  LED3 = LED - 5mm [color="Red (633nm)" package="5 mm [THT]"]
  LED4 = LED - 5mm [color="Red (633nm)" package="5 mm [THT]"]
  LED5 = LED - 5mm [color="Red (633nm)" package="5 mm [THT]"]
  LED6 = LED - 5mm [color="Red (633nm)" package="5 mm [THT]"]
  LED7 = LED - 5mm [color="Green (555nm)" package="5 mm [THT]"]
  LED8 = LED - 5mm [color="Green (555nm)" package="5 mm [THT]"]
  LED9 = LED - 5mm [color="Blue (505nm)" package="5 mm [THT]"]
  R1 = Resistor [tolerance=±5% resistance=330 package=THT]
  R2 = Resistor [tolerance=±5% resistance=330 package=THT]
  R3 = Resistor [tolerance=±5% resistance=330 package=THT]
  R4 = Resistor [tolerance=±5% resistance=330 package=THT]
  R5 = Resistor [tolerance=±5% resistance=330 package=THT]
  R6 = Resistor [tolerance=±5% resistance=330 package=THT]
  R7 = Resistor [tolerance=±5% resistance=330 package=THT]
  R8 = Resistor [tolerance=±5% resistance=330 package=THT]
  R9 = Resistor [tolerance=±5% resistance=330 package=THT]
  SP1 = SPEAKER [package=pcb_mount_speaker]

nets:
  N1: Componente1.D8, R6.Pin_0
  N2: Componente1.D9_PWM, R7.Pin_0
  N3: Componente1.D10_PWM/SS, R8.Pin_0
  N4: Componente1.D11_PWM/MOSI, R9.Pin_0
  N5: Componente1.D12/MISO, SP1.-
  N6: Componente1.D2, R2.Pin_0
  N7: Componente1.D3_PWM, R3.Pin_0
  N8: Componente1.D4, R4.Pin_0
  N9: Componente1.D5_PWM, R1.Pin_0
  N10: Componente1.D7, R5.Pin_0
  N11: Componente1.GND, LED1.cathode, LED2.cathode, LED3.cathode, LED4.cathode, LED5.cathode, LED6.cathode, LED7.cathode, LED8.cathode, LED9.cathode, SP1.+
  N12: LED1.anode, R8.Pin_1
  N13: LED2.anode, R7.Pin_1
  N14: LED3.anode, R6.Pin_1
  N15: LED4.anode, R2.Pin_1
  N16: LED5.anode, R3.Pin_1
  N17: LED6.anode, R4.Pin_1
  N18: LED7.anode, R1.Pin_1
  N19: LED8.anode, R9.Pin_1
  N20: LED9.anode, R5.Pin_1
