# Fritzing sketch esquema_semaforo (saved by Fritzing 0.9.3b)
breadboards: 1

parts:
  R1 = Resistor [tolerance=±5% resistance=330 package=THT]
  R2 = Resistor [tolerance=±5% resistance=330 package=THT]
  R3 = Resistor [tolerance=±5% resistance=330 package=THT]
  Componente1 = Arduino Uno (Rev3)
  LED2 = LED - 5mm [color="Red (633nm)" package="5 mm [THT]"]
  LED3 = LED - 5mm [color="Yellow (595nm)" package="5 mm [THT]"]
  LED4 = LED - 5mm [color="Green (570nm)" package="5 mm [THT]"]
  R4 = Resistor [tolerance=±5% resistance=330 package=THT]
  R5 = Resistor [tolerance=±5% resistance=330 package=THT]
  R6 = Resistor [tolerance=±5% resistance=330 package=THT]
  LED5 = LED - 5mm [color="Red (633nm)" package="5 mm [THT]"]
  LED6 = LED - 5mm [color="Green (570nm)" package="5 mm [THT]"]
  LED7 = LED - 5mm [color="Yellow (595nm)" package="5 mm [THT]"]

nets:
  N1: R1.Pin_0, R2.Pin_0, R3.Pin_0, Componente1.GND, R4.Pin_0, R5.Pin_0, R6.Pin_0
  N2: R1.Pin_1, LED2.cathode
  N3: R2.Pin_1, LED3.cathode
  N4: R3.Pin_1, LED4.cathode
  N5: Componente1.D11_PWM/MOSI, LED4.anode
  N6: Componente1.D12/MISO, LED3.anode
  N7: Componente1.D13/SCK, LED2.anode
  N8: Componente1.D2, LED6.anode
  N9: Componente1.D3_PWM, LED7.anode
  N10: Componente1.D4, LED5.anode
  N11: R4.Pin_1, LED5.cathode
  N12: R5.Pin_1, LED7.cathode
  N13: R6.Pin_1, LED6.cathode
